// Logisim project (1to2)DeMultiplexer.circ as structural Verilog: 1 circuit, main circuit main
module main (
  input  I,
  input  So,
  output Yo,
  output Y1
);

  wire not_1_out;

  not not_1 (not_1_out, So);
  and and_1 (Yo, I, not_1_out);
  and and_2 (Y1, I, So);

  // Notes on the sheet:
  //   I
  //   So
  //   I.So'
  //   I.So
  //   1 to 2 Demultiplexer
endmodule
