// Logisim project (1to4)DEMULTIPLEXER.circ as structural Verilog: 1 circuit, main circuit main
module main (
  input  Do,
  input  S1_prime,
  input  So_prime,
  input  D1,
  input  D2,
  input  D3,
  output Do_S1_prime_So_prime,
  output Y1,
  output D2_S1So_prime,
  output Y3
);

  wire not_1_out, not_2_out;

  not not_1 (not_1_out, S1_prime);
  not not_2 (not_2_out, So_prime);
  and and_1 (Do_S1_prime_So_prime, Do, not_1_out, not_2_out);
  and and_2 (Y1, D1, not_1_out, So_prime);
  and and_3 (D2_S1So_prime, D2, S1_prime, not_2_out);
  and and_4 (Y3, D3, S1_prime, So_prime);

  // Notes on the sheet:
  //   D1.S1'So
  //   D3.S1.So
  //   Yo
  //   Y2
  //   (1 to 4)DEMULTIPLEXER
endmodule
