// Logisim project (2to1)Multiplexer.circ as structural Verilog: 1 circuit, main circuit main
module main (
  input  D1,
  input  S,
  input  Do,
  output D1_S_Do_S_prime
);

  wire and_1_out, and_2_out, not_1_out;

  not not_1 (not_1_out, S);
  and and_1 (and_1_out, D1, S);
  and and_2 (and_2_out, Do, not_1_out);
  or or_1 (D1_S_Do_S_prime, and_1_out, and_2_out);

  // Notes on the sheet:
  //   MULTIPLEXER
  //   Y
endmodule
