// Logisim project (4to1)MULTIPLEXER.circ as structural Verilog: 1 circuit, main circuit main
module main (
  input  Do,
  input  S1_prime,
  input  So_prime,
  input  D1,
  input  D2,
  input  D3,
  output out_7
);

  wire and_1_out, and_2_out, and_3_out, and_4_out, not_1_out, not_2_out;

  not not_1 (not_1_out, S1_prime);
  not not_2 (not_2_out, So_prime);
  and and_1 (and_1_out, Do, not_1_out, not_2_out);
  and and_2 (and_2_out, D1, not_1_out, So_prime);
  and and_3 (and_3_out, D2, S1_prime, not_2_out);
  and and_4 (and_4_out, D3, S1_prime, So_prime);
  or or_1 (out_7, and_1_out, and_2_out, and_3_out, and_4_out);

  // Notes on the sheet:
  //   Y= Do.S1'So'+D1.S1'So+D2.S1So'+D3.S1.So
  //   (4 to1)MULTIPLEXER
endmodule
