// Logisim project 2to1Multiplexer.circ as structural Verilog: 1 circuit, main circuit main
module main (
  input  A,
  input  SUM,
  input  B,
  output out_4
);

  wire and_1_out, and_2_out, not_1_out;

  not not_1 (not_1_out, SUM);
  and and_1 (and_1_out, A, SUM);
  and and_2 (and_2_out, B, not_1_out);
  or or_1 (out_4, and_1_out, and_2_out);

  // Notes on the sheet:
  //   MULTIPLEXER
endmodule
