// Logisim project adders.circ as structural Verilog: 1 circuit, main circuit main
module main (
  input  A,
  input  B,
  input  A_2,
  input  B_2,
  input  Cin,
  output out_6,
  output out_7,
  output A_prime_B_AB_prime,
  output AB_BC_CA
);

  wire and_1_out, and_2_out, and_4_out, and_5_out, and_6_out, and_7_out, and_8_out, not_1_out, not_2_out,
       not_3_out, not_4_out;

  not not_1 (not_1_out, A);
  and and_1 (and_1_out, not_1_out, B);
  and and_2 (and_2_out, A, not_2_out);
  not not_2 (not_2_out, B);
  and and_3 (out_7, A, B);
  not not_3 (not_3_out, A_2);
  not not_4 (not_4_out, B_2);
  and and_4 (and_4_out, not_3_out, B_2, Cin);
  and and_5 (and_5_out, A_2, not_4_out);
  and and_6 (and_6_out, A_2, B_2);
  and and_7 (and_7_out, B_2, Cin);
  and and_8 (and_8_out, Cin, A_2);
  or or_1 (out_6, and_1_out, and_2_out);
  or or_2 (A_prime_B_AB_prime, and_4_out, and_5_out);
  or or_3 (AB_BC_CA, and_6_out, and_7_out, and_8_out);

  // Notes on the sheet:
  //   AB
  //   A'B+AB'
  //   HALF ADDR
  //   FULL ADDER
endmodule
